// Logisim project IC7043.circ as structural Verilog: 1 circuit, main circuit main
module main (
  input  A,
  input  B,
  input  C,
  output F
);

  wire A_prime_C_AB_prime_out, A_prime_C_out, AB_prime_out, BC_out, not_1_out, not_2_out;

  not not_1 (not_1_out, A);
  not not_2 (not_2_out, B);
  and A_prime_C (A_prime_C_out, not_1_out, C);
  and AB_prime (AB_prime_out, A, not_2_out);
  and BC (BC_out, B, C);
  or A_prime_C_AB_prime (A_prime_C_AB_prime_out, A_prime_C_out, AB_prime_out);
  or or_1 (F, A_prime_C_AB_prime_out, BC_out);
endmodule
